# Fritzing sketch sigfox_talking_plant (saved by Fritzing 0.9.2b)
breadboards: 1

parts:
  R1 = PHOTOCELL [package=photocell]
  R2 = Resistor [tolerance=±5% resistance=10k package="0805 [SMD]"]
  Composant1 = Arduino Uno (Rev3)
  PART1 = SparkFun Soil Moisture Sensor [part_number=SEN-13322]

nets:
  N1: R1.P$1, Composant1.5V
  N2: R1.P$2, R2.Pin_0, Composant1.A0
  GND: R2.Pin_1, Composant1.GND, PART1.GND
  N3: Composant1.A1, PART1.SIG
  3V3: Composant1.3V3, PART1.VCC

custom parts:
  SparkFun Soil Moisture Sensor: The SparkFun Soil Moisture Sensor is a simple breakout for measuring the moisture in soil and similar materials.
